// Logisim project dineflow_final.circ as structural Verilog: 5 circuits, main circuit main
module main (
  input  in_1,
  input  in_2,
  input  in_3,
  input  in_4,
  input  [3:0] in_5,
  input  [3:0] in_6,
  input  [3:0] in_7,
  input  [3:0] in_8,
  input  in_9,
  input  in_10,
  input  in_11,
  input  in_12,
  input  in_13,
  input  in_14,
  input  in_15,
  input  in_16,
  input  [3:0] in_17,
  input  [3:0] in_18,
  input  [3:0] in_19,
  input  [3:0] in_20,
  input  [1:0] TABLE_1,
  input  [1:0] TABLE_2,
  input  CHOOSE_TABLE,
  input  ENABLE,
  input  [3:0] in_25,
  input  [3:0] in_26,
  input  [3:0] in_27,
  input  [3:0] in_28,
  input  [1:0] in_29,
  input  in_30,
  input  in_31,
  output [3:0] out_32,
  output [3:0] out_33,
  output [3:0] out_34,
  output [3:0] out_35,
  output [5:0] out_36,
  output [5:0] out_37
);

  wire clock_1_out, decoder_1_out0, decoder_1_out1, decoder_1_out2, decoder_1_out3,
       inventory_1_comparator_output, inventory_2_comparator_output, inventory_3_comparator_output,
       inventory_4_comparator_output, not_1_out, not_2_out, or_1_out, or_2_out, or_3_out, queue_1_out_0,
       queue_1_out_1, queue_1_out_2, queue_2_out_0, queue_2_out_1, queue_2_out_2;
  wire [1:0] and_1_out, demultiplexer_1_out0, demultiplexer_1_out1, multiplexer_1_out,
       timer_1__2_bit_item_output;

  Multiplexer #(.width(2)) multiplexer_1 (
    .in0(TABLE_1), .in1(TABLE_2), .out(multiplexer_1_out), .sel(CHOOSE_TABLE), .en(ENABLE));
  Decoder #(.select(2)) decoder_1 (
    .out0(decoder_1_out0), .out1(decoder_1_out1), .out2(decoder_1_out2), .out3(decoder_1_out3),
    .sel(multiplexer_1_out), .en(ENABLE));
  inventory inventory_1 (
    .Counter_enabler(ENABLE), .Item_Count(in_5), .Decrement_enabler(in_1), .Manual_Clock_set(in_9),
    .Clear_counter(in_13), .set_to_0(4'b0000), .set_to_item_1(in_17), .Decoder_input(decoder_1_out0),
    .Item_available(out_32), .comparator_output(inventory_1_comparator_output));  // open: Counter_carry
  Demultiplexer #(.width(2)) demultiplexer_1 (
    .out0(demultiplexer_1_out0), .out1(demultiplexer_1_out1), .in(timer_1__2_bit_item_output),
    .sel(CHOOSE_TABLE), .en(ENABLE));
  inventory inventory_2 (
    .Counter_enabler(ENABLE), .Item_Count(in_6), .Decrement_enabler(in_2), .Manual_Clock_set(in_10),
    .Clear_counter(in_14), .set_to_0(4'b0000), .set_to_item_1(in_18), .Decoder_input(decoder_1_out1),
    .Item_available(out_33), .comparator_output(inventory_2_comparator_output));  // open: Counter_carry
  not not_1 (not_1_out, demultiplexer_1_out0[1]);
  not not_2 (not_2_out, demultiplexer_1_out1[1]);
  or or_1 (or_1_out, inventory_1_comparator_output, inventory_2_comparator_output, inventory_3_comparator_output, inventory_4_comparator_output);
  or or_2 (or_2_out, demultiplexer_1_out0[0], demultiplexer_1_out0[1]);
  or or_3 (or_3_out, demultiplexer_1_out1[0], demultiplexer_1_out1[1]);
  queue queue_1 (
    .Clk(or_2_out), .BIT_0(demultiplexer_1_out0[0]), .BIT_1(not_1_out), .BIT_2(demultiplexer_1_out0[1]),
    .out_0(queue_1_out_0), .OUT_1(queue_1_out_1), .OUT_2(queue_1_out_2));
  queue queue_2 (
    .Clk(or_3_out), .BIT_0(demultiplexer_1_out1[0]), .BIT_1(not_2_out), .BIT_2(demultiplexer_1_out1[1]),
    .out_0(queue_2_out_0), .OUT_1(queue_2_out_1), .OUT_2(queue_2_out_2));
  inventory inventory_3 (
    .Counter_enabler(ENABLE), .Item_Count(in_7), .Decrement_enabler(in_3), .Manual_Clock_set(in_11),
    .Clear_counter(in_15), .set_to_0(4'b0000), .set_to_item_1(in_19), .Decoder_input(decoder_1_out2),
    .Item_available(out_34), .comparator_output(inventory_3_comparator_output));  // open: Counter_carry
  and and_1 (and_1_out[0], or_1_out, multiplexer_1_out[0]);
  and and_2 (and_1_out[1], or_1_out, multiplexer_1_out[1]);
  billing billing_1 (
    .ENABLE_BILL(ENABLE), .C_MSB(queue_1_out_2), .CLK(or_2_out), .B(queue_1_out_1), .A_LSB(queue_1_out_0),
    .FINAL_BILL(out_36), .CLEAR_BILL(in_30));
  billing billing_2 (
    .ENABLE_BILL(ENABLE), .C_MSB(queue_2_out_2), .CLK(or_3_out), .B(queue_2_out_1), .A_LSB(queue_2_out_0),
    .FINAL_BILL(out_37), .CLEAR_BILL(in_31));
  Clock clock_1 (.out(clock_1_out));
  timer timer_1 (
    .item_number_1__time_for_prep(in_28), .item_number_2__time_for_prep(in_27),
    .item_number_3_time_for_prep(in_26), .item_number_4__time_for_prep(in_25), .item_input(and_1_out),
    .condition__always_11(in_29), .always_1_2(1'b1), .in_9(clock_1_out), .always_1(1'b1),
    .comparator_conmdition__be_equal_to_0(4'b0000), ._2_bit_item_output(timer_1__2_bit_item_output));  // open: out_11
  inventory inventory_4 (
    .Counter_enabler(ENABLE), .Item_Count(in_8), .Decrement_enabler(in_4), .Manual_Clock_set(in_12),
    .Clear_counter(in_16), .set_to_0(4'b0000), .set_to_item_1(in_20), .Decoder_input(decoder_1_out3),
    .Item_available(out_35), .comparator_output(inventory_4_comparator_output));  // open: Counter_carry

  // Notes on the sheet:
  //   ITEM 1 - INVENTORY COUNT
  //   ITEM 2 - INVENTORY COUNT
  //   DINEFLOW- DIGITAL RESTAURANT MANAGEMENT SYSTEM
  //   ITEM3 - INVENTORY COUNT
  //   TOTAL BILL- TABLE 1
  //   TOTAL BILL - TABLE 2
  //   ITEM 4 - INVENTORY COUNT
  //   TIME FOR EACH ITEM
  //   TEAM MEMBERS-
  //   1) Rakshith Ashok Kumar - 231CS147
  //   2) Utsav Singh Bhamra - 231CS161
  //   3) Akshaj PVY - 231CS109
  //   INSTRUCTIONS - 
  //   1) Enable the multiplexer and decoder and set the table number in the mux
  //   2) Enable all the inventory modules corresponding to each item in the menu.
  //   5) Enable the timer module and set the time taken for each item through the 4 bit inputs 
  //   6) Run the clocks once your order is ready and in the queue to get bill
  //   3) Set the item count input in each inventory module to the number of items available in the kitchen.
  //   4) Set the 4 bit comparator input to item count +1 and then enable decrement in all inventory modues.
endmodule

// Inventory
module inventory (
  input  Counter_enabler,
  input  [3:0] Item_Count,
  input  Decrement_enabler,
  input  Manual_Clock_set,
  input  Clear_counter,
  input  [3:0] set_to_0,
  input  [3:0] set_to_item_1,
  input  Decoder_input,
  output [3:0] Item_available,
  output Counter_carry,
  output comparator_output
);

  wire comparator_1_lt, comparator_2_gt, or_1_out;

  Counter #(.width(4), .max('hf)) counter_1 (
    .load(Counter_enabler), .D(Item_Count), .count(Decrement_enabler), .Q(Item_available),
    .carry(Counter_carry), .clk(or_1_out), .clr(Clear_counter));
  or or_1 (or_1_out, Manual_Clock_set, comparator_output);
  Comparator #(.width(4), .mode("unsigned")) comparator_1 (
    .a(set_to_0), .b(Item_available), .lt(comparator_1_lt));  // open: gt, eq
  Comparator #(.width(4), .mode("unsigned")) comparator_2 (
    .a(set_to_item_1), .b(Item_available), .gt(comparator_2_gt));  // open: eq, lt
  and and_1 (comparator_output, comparator_1_lt, comparator_2_gt, Decoder_input);

  // Notes on the sheet:
  //   INVENTORY MODULE
  //   - COMPARATOR TO CHECK IF ITEM IS AVAILABLE
  //   - REGISTER TO STORE ITEM COUNT
endmodule

// QUEUE
module queue (
  input  Clk,
  input  BIT_0,
  input  BIT_1,
  input  BIT_2,
  output out_0,
  output OUT_1,
  output OUT_2
);

  wire d_ff_1_q, d_ff_2_q, d_ff_3_q, d_ff_4_q, d_ff_5_q, d_ff_6_q, d_ff_7_q, d_ff_8_q, d_ff_9_q;

  D_Flip_Flop d_ff_1 (.clk(Clk), .D(BIT_0), .Q(d_ff_1_q));  // open: Qn, preset, en, reset
  D_Flip_Flop d_ff_2 (.clk(Clk), .D(BIT_1), .Q(d_ff_2_q));  // open: Qn, preset, en, reset
  D_Flip_Flop d_ff_3 (.clk(Clk), .D(BIT_2), .Q(d_ff_3_q));  // open: Qn, preset, en, reset
  D_Flip_Flop d_ff_4 (.clk(Clk), .D(d_ff_1_q), .Q(d_ff_4_q));  // open: Qn, preset, en, reset
  D_Flip_Flop d_ff_5 (.clk(Clk), .D(d_ff_2_q), .Q(d_ff_5_q));  // open: Qn, preset, en, reset
  D_Flip_Flop d_ff_6 (.clk(Clk), .D(d_ff_3_q), .Q(d_ff_6_q));  // open: Qn, preset, en, reset
  D_Flip_Flop d_ff_7 (.clk(Clk), .D(d_ff_4_q), .Q(d_ff_7_q));  // open: Qn, preset, en, reset
  D_Flip_Flop d_ff_8 (.clk(Clk), .D(d_ff_5_q), .Q(d_ff_8_q));  // open: Qn, preset, en, reset
  D_Flip_Flop d_ff_9 (.clk(Clk), .D(d_ff_6_q), .Q(d_ff_9_q));  // open: Qn, preset, en, reset
  D_Flip_Flop d_ff_10 (.clk(Clk), .D(d_ff_7_q), .Q(out_0));  // open: Qn, preset, en, reset
  D_Flip_Flop d_ff_11 (.clk(Clk), .D(d_ff_8_q), .Q(OUT_1));  // open: Qn, preset, en, reset
  D_Flip_Flop d_ff_12 (.clk(Clk), .D(d_ff_9_q), .Q(OUT_2));  // open: Qn, preset, en, reset

  // Notes on the sheet:
  //   ORDER QUEUE USING SHIFT REGISTERS
  //   - TAKES 3 BIT INPUT AND GIVES 3 BIT OUTPUT 
  //   - IMPLEMENTED USING D FLIP FLOPS
endmodule

// BILLING
module billing (
  input  ENABLE_BILL,
  input  C_MSB,
  input  CLEAR_BILL,
  input  CLK,
  input  B,
  input  A_LSB,
  output [5:0] FINAL_BILL
);

  wire [5:0] adder_1_out, bit_extender_1_out;

  assign bit_extender_1_out = {{3{1'b0}}, {C_MSB, B, A_LSB}};  // Bit_Extender bit_extender_1
  Adder #(.width(6)) adder_1 (.a(FINAL_BILL), .b(bit_extender_1_out), .out(adder_1_out));  // open: cin, cout
  Register #(.width(6)) register_1 (.D(adder_1_out), .en(ENABLE_BILL), .Q(FINAL_BILL), .clk(CLK), .clr(CLEAR_BILL));

  // Notes on the sheet:
  //   BILLING MODULE TO CALCULATE TOTAL ORDER VALUE
  //   - ADDER TO ADD ORDER PRICES
  //   - REGISTER TO STORE TOTAL BILL
endmodule

// TIMER
module timer (
  input  always_1,
  input  [3:0] item_number_1__time_for_prep,
  input  [3:0] comparator_conmdition__be_equal_to_0,
  input  [1:0] condition__always_11,
  input  [3:0] item_number_2__time_for_prep,
  input  [3:0] item_number_3_time_for_prep,
  input  always_1_2,
  input  [3:0] item_number_4__time_for_prep,
  input  in_9,
  input  [1:0] item_input,
  output [3:0] out_11,
  output [1:0] _2_bit_item_output
);

  wire comparator_1_eq;
  wire [1:0] bit_extender_1_out, multiplier_1_out;
  wire [3:0] counter_1_q;

  Multiplexer #(.select(2), .width(4)) multiplexer_1 (
    .in0(item_number_1__time_for_prep), .in1(item_number_2__time_for_prep),
    .in2(item_number_3_time_for_prep), .in3(item_number_4__time_for_prep), .out(out_11), .sel(item_input));  // open: en
  Counter #(.width(4), .max('hf), .ongoal("load")) counter_1 (
    .load(always_1), .D(out_11), .count(always_1_2), .Q(counter_1_q), .clk(in_9));  // open: carry, clr
  Comparator #(.width(4), .mode("unsigned")) comparator_1 (
    .a(comparator_conmdition__be_equal_to_0), .b(counter_1_q), .eq(comparator_1_eq));  // open: gt, lt
  assign bit_extender_1_out = {{1{1'b0}}, comparator_1_eq};  // Bit_Extender bit_extender_1
  Multiplier #(.width(2)) multiplier_1 (
    .a(condition__always_11), .b(bit_extender_1_out), .out(multiplier_1_out));  // open: cin, cout
  assign _2_bit_item_output = multiplier_1_out & item_input;  // AND_Gate and_1, 2 bits wide

  // Notes on the sheet:
  //   item number (2 bit input)
  //   prep time for item 
  //   down counter 
  //   - Stores time to prepare each item
  //   TIMER MODULE
  //   - Uses a Down Counter to count till 0 and detect order readiness
endmodule
